# Fritzing sketch schema (saved by Fritzing 0.9.3b)

parts:
  Composant1 = Arduino Nano (Rev3.0)
  Composant2 = Bluetooth HC-05 Macho
  ZS-042_RTC1 = ZS-042 RTC Module
  J1 = Power Jack [package=power_jack_pth]
  Composant3 = LED Matrix - Serial Interface - Red/Green/Blue

nets:
  N1: Composant1.D1/TX, Composant2.TXD
  N2: Composant1.D0/RX, Composant2.RXD
  GND: Composant1.GND, Composant2.GND, ZS-042_RTC1.GND, J1.GND, J1.GNDBREAK, Composant3.GND
  N3: Composant1.D6, Composant3.DIN
  VCC: Composant1.5V, Composant2.VCC, ZS-042_RTC1.VCC, J1.PWR, Composant3.VCC
  N4: Composant1.A5, ZS-042_RTC1.SCL
  N5: Composant1.A4, ZS-042_RTC1.SDA

custom parts:
  LED Matrix - Serial Interface - Red/Green/Blue: Description: This is a large sized RGB LED Matrix with a backpack that has been designed to take SPI serial input and display any graphics you pass it. All the refreshing and communication control is taken care of by the backpack. It's even reprogrammable! 7 software selectable colors are available! Unit comes with a Red/Green/Blue LED Matrix assembled with a RGB Matrix Backpack Controller.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
